# Fritzing sketch CircuitDesign (saved by Fritzing 0.9.3b)
breadboards: 1

parts:
  Part1 = RFID-RC522 [part_number=101218]
  LED1 = smd LED [color="Red (633nm)" package="0805 [SMD]"]
  R3 = Resistor [tolerance=±5% resistance=220 package="2010 [SMD]"]
  U3 = ESP32-38PinWide [part_number=ESP32-38PinWide]
  R4 = Resistor [tolerance=±5% resistance=220 package="2010 [SMD]"]
  S1 = Pushbutton [package="[THT]"]
  R5 = Resistor [tolerance=±5% resistance=220 package="2010 [SMD]"]
  LED3 = LED - 5mm [color="Green (560nm)" package="5 mm [THT]"]

nets:
  N1: Part1.SDA, U3.GPIO5
  N2: Part1.SCK, U3.GPIO18
  N3: Part1.MOSI, U3.GPIO23
  N4: Part1.MISO, U3.GPIO19
  N5: Part1.GND, LED1.cathode, R5.Pin_0, LED3.cathode
  N6: Part1.RST, U3.GPIO22
  N7: Part1.3.3V, U3.3.3, S1.Pin_1, S1.Pin_2
  N8: LED1.anode, R3.Pin_0
  N9: R3.Pin_1, U3.GPIO0
  N10: U3.GPIO8, R4.Pin_1
  N11: U3.GPIO15, S1.Pin_3, S1.Pin_4, R5.Pin_1
  N12: R4.Pin_0, LED3.anode

custom parts:
  ESP32-38PinWide: Generic 38-Pin ESP32 with wide format (only access to one side of pins on a breadboard) based on Stephen Lilley's HiLetgo ESP-WROOM-32 ESP32 ESP-32S Development Board.
